// Logisim project lab2.circ as structural Verilog: 2 circuits, main circuit Problem1
module Problem1 (
  input  A,
  input  A_2,
  input  B,
  input  B_2,
  input  C,
  input  C_2
);

  wire A_prime_B_prime_C_out, A_prime_B_prime_out, AB_2_out, AB_C_2_out, AB_C_out, AB_out, AB_prime_C_out,
       AB_prime_out, not_1_out, not_2_out, not_3_out, or_1_out, or_2_out, or_3_out, or_4_out, or_5_out,
       or_6_out;

  and AB_C (AB_C_out, C, AB_out);
  or or_1 (or_1_out, AB_C_out, AB_out);
  and AB (AB_out, A, B);
  or or_2 (or_2_out, A, or_4_out);
  or or_3 (or_3_out, or_1_out, or_2_out);
  LED F (.in(or_3_out));
  or or_4 (or_4_out, C, B);
  not not_1 (not_1_out, A_2);
  not not_2 (not_2_out, B_2);
  not not_3 (not_3_out, C_2);
  and A_prime_B_prime (A_prime_B_prime_out, not_1_out, not_2_out);
  and A_prime_B_prime_C (A_prime_B_prime_C_out, A_prime_B_prime_out, C_2);
  and AB_prime (AB_prime_out, A_2, not_2_out);
  and AB_prime_C (AB_prime_C_out, AB_prime_out, C_2);
  or or_5 (or_5_out, A_prime_B_prime_C_out, AB_prime_C_out);
  or or_6 (or_6_out, or_5_out, AB_C_2_out);
  LED G (.in(or_6_out));
  and AB_2 (AB_2_out, A_2, B_2);
  and AB_C_2 (AB_C_2_out, AB_2_out, C_2);

  // Notes on the sheet:
  //   Part A
  //   Part B
endmodule

module Problem_2 (
  input  Car_0,
  input  Car_1,
  input  Car_2,
  input  Car_3,
  input  Car_4,
  input  Car_5,
  input  Car_6
);

  wire _0_2_out, _0_out, _1_2_out, _1_3_out, _1_out, _2_2_out, _2_3_out, _2_out, _3_out, _4_2_out, _4_3_out,
       _4_out, _5_out, _6_out, B_out, LB_out, LT_out, M_out, not_1_out, not_2_out, not_3_out, RB_out, RT_out,
       T_out;

  or _2 (_2_out, Car_2, Car_3, Car_6);
  or _1 (_1_out, Car_1, Car_3, Car_5);
  or _4 (_4_out, Car_4, Car_5, Car_6);
  or _0 (_0_out, Car_6, Car_5, Car_4, Car_3, Car_2, Car_1, Car_0);
  and _1_2 (_1_2_out, _1_out, _0_out);
  not not_1 (not_1_out, _1_2_out);
  and _2_2 (_2_2_out, _2_out, _0_out);
  and _4_2 (_4_2_out, _4_out, _0_out);
  not not_2 (not_2_out, _4_2_out);
  not not_3 (not_3_out, _2_2_out);
  and _0_2 (_0_2_out, _0_out, not_1_out, not_3_out, not_2_out);
  and _1_3 (_1_3_out, _1_2_out, not_3_out, not_2_out);
  and _2_3 (_2_3_out, not_1_out, _2_2_out, not_2_out);
  and _3 (_3_out, _1_2_out, _2_2_out, not_2_out);
  and _4_3 (_4_3_out, not_1_out, not_3_out, _4_2_out);
  and _5 (_5_out, _1_2_out, not_3_out, _4_2_out);
  and _6 (_6_out, not_1_out, _2_2_out, _4_2_out);
  or LB (LB_out, _0_2_out, _2_3_out, _6_out);
  or B (B_out, _0_2_out, _2_3_out, _3_out, _5_out, _6_out);
  or M (M_out, _2_3_out, _3_out, _4_3_out, _5_out, _6_out);
  _7_Segment_Display u_7_segment_display_1 (
    .g(M_out), .f(LT_out), .a(T_out), .b(RT_out), .e(LB_out), .d(B_out), .c(RB_out));  // open: dp
  or LT (LT_out, _0_2_out, _4_3_out, _5_out, _6_out);
  or T (T_out, _0_2_out, _2_3_out, _3_out, _5_out, _6_out);
  or RT (RT_out, _0_2_out, _1_3_out, _2_3_out, _3_out, _4_3_out);
  or RB (RB_out, _0_2_out, _1_3_out, _3_out, _4_3_out, _5_out, _6_out);

  // Notes on the sheet:
  //   Encoder
  //   Bus
  //   Decoder
endmodule
