// Logisim project lab4.circ as structural Verilog: 2 circuits, main circuit main
module main (
  input  in_1,
  input  in_2,
  input  in_3,
  input  in_4,
  input  in_5,
  input  in_6,
  input  in_7,
  input  in_8,
  input  A0,
  input  A1,
  input  A2,
  input  A3,
  input  A4,
  input  A5,
  input  A6,
  input  A7,
  input  C0,
  input  C1,
  input  C2,
  input  C3,
  input  D0,
  input  D1,
  input  D2,
  input  D3,
  input  D4,
  input  D5,
  input  D6,
  input  D7,
  output out_29,
  output out_30,
  output out_31,
  output D0O,
  output D1O,
  output D2O,
  output D3O,
  output D4O,
  output D5O,
  output D6O,
  output D7O
);

  wire IO_R_out, IO_W_out, nor_1_out, not_1_out, not_2_out, O__A_out, or_1_out, or_2_out, or_3_out,
       RAM_R_out, RAM_W_out, ROM_R_out;
  wire [7:0] controlled_buffer_1_out, controlled_buffer_4_out, i_o_1_do;

  assign controlled_buffer_1_out = nor_1_out ? {D7, D6, D5, D4, D3, D2, D1, D0} : 8'bz;  // Controlled_Buffer controlled_buffer_1
  not not_1 (not_1_out, nor_1_out);
  assign {D7O, D6O, D5O, D4O, D3O, D2O, D1O, D0O} = not_1_out ? controlled_buffer_1_out : 8'bz;  // Controlled_Buffer controlled_buffer_2
  nor nor_1 (nor_1_out, ROM_R_out, O__A_out, RAM_R_out, IO_R_out);
  or or_1 (or_1_out, ROM_R_out, O__A_out);
  and ROM_R (ROM_R_out, C0, ~C1, ~C2, ~C3);  // AND_Gate
  ROM rom_1 (.addr({A7, A6, A5, A4, A3, A2, A1, A0}), .data(controlled_buffer_1_out), .sel(or_1_out));
  and O__A (O__A_out, ~C0, C1, C2, ~C3);  // AND_Gate
  and RAM_R (RAM_R_out, ~C0, C1, ~C2, ~C3);  // AND_Gate
  or or_2 (or_2_out, RAM_R_out, or_3_out);
  not not_2 (not_2_out, or_3_out);
  or or_3 (or_3_out, O__A_out, RAM_W_out);
  and RAM_W (RAM_W_out, C0, C1, ~C2, ~C3);  // AND_Gate
  RAM #(.bus("asynch")) ram_1 (
    .addr({A7, A6, A5, A4, A3, A2, A1, A0}), .data(controlled_buffer_1_out), .sel(or_2_out), .ld(not_2_out));  // open: clr
  I_O i_o_1 (
    .DO(i_o_1_do), .DI(controlled_buffer_4_out), .Write(IO_W_out), .Read(IO_R_out),
    .A({A7, A6, A5, A4, A3, A2, A1, A0}), .DOS(in_1), .DSBF(in_2), .BELL(out_29), .ER(in_3), .DLA(out_30),
    .DC(in_4), .BA(out_31), .KIC(in_5), .DLC(in_6), .BP(in_7), .CM(in_8));
  and IO_R (IO_R_out, ~C0, ~C1, C2, ~C3);  // AND_Gate
  and IO_W (IO_W_out, C0, ~C1, C2, ~C3);  // AND_Gate
  assign controlled_buffer_1_out = IO_R_out ? i_o_1_do : 8'bz;  // Controlled_Buffer controlled_buffer_3
  assign controlled_buffer_4_out = IO_W_out ? controlled_buffer_1_out : 8'bz;  // Controlled_Buffer controlled_buffer_4

  // Notes on the sheet:
  //   contents of rom_1 (hex, n*v repeats v):
  //   0 1 2 3 4 5 6 7 8 9 a b c d e f
endmodule

module I_O (
  input  DOS,
  input  DSBF,
  input  ER,
  input  DC,
  input  KIC,
  input  DLC,
  input  BP,
  input  [7:0] DI,
  input  CM,
  input  Write,
  input  Read,
  input  [7:0] A,
  output [7:0] DO,
  output BELL,
  output DLA,
  output BA
);

  wire and_1_out, and_2_out, and_3_out, not_1_out, not_2_out, not_3_out, not_4_out, not_5_out, not_6_out,
       not_7_out, not_8_out, not_9_out, not_10_out;
  wire [7:0] controlled_buffer_2_out, controlled_buffer_3_out;
  wire [7:3] register_1_q;

  assign DO = Read ? controlled_buffer_3_out : 8'bz;  // Controlled_Buffer controlled_buffer_1
  assign controlled_buffer_2_out = Write ? DI : 8'bz;  // Controlled_Buffer controlled_buffer_2
  not not_1 (not_1_out, Read);
  not not_2 (not_2_out, Write);
  not not_3 (not_3_out, A[0]);
  not not_4 (not_4_out, A[1]);
  not not_5 (not_5_out, A[2]);
  not not_6 (not_6_out, A[3]);
  not not_7 (not_7_out, A[4]);
  not not_8 (not_8_out, A[5]);
  not not_9 (not_9_out, A[6]);
  not not_10 (not_10_out, A[7]);
  Register #(.trigger("high")) register_1 (
    .D({{5{1'b0}}, controlled_buffer_2_out[2:0]}), .Q({register_1_q, BA, DLA, BELL}), .clk(and_1_out));  // open: en, clr
  and and_1 (and_1_out, Write, not_1_out, not_3_out, not_4_out, not_5_out, not_6_out, A[4], not_8_out, not_9_out, not_10_out);
  assign controlled_buffer_3_out = and_2_out ? {register_1_q, BA, DLA, BELL} : 8'bz;  // Controlled_Buffer controlled_buffer_3
  and and_2 (and_2_out, not_2_out, Read, not_3_out, not_4_out, not_5_out, not_6_out, A[4], not_8_out, not_9_out, not_10_out);
  assign controlled_buffer_3_out = and_3_out ? {CM, BP, DLC, KIC, DC, ER, DSBF, DOS} : 8'bz;  // Controlled_Buffer controlled_buffer_4
  and and_3 (and_3_out, not_2_out, Read, A[0], A[1], A[2], A[3], A[4], A[5], A[6], A[7]);
endmodule
