// Logisim project problem1.circ as structural Verilog: 1 circuit, main circuit main
module main (
  input  in_1,
  input  in_2
);

  wire and_1_out, and_2_out, and_3_out, and_4_out, and_5_out, and_6_out, and_7_out, and_8_out, and_9_out,
       and_10_out, and_11_out, and_12_out, and_13_out, and_14_out, and_15_out, and_16_out, and_17_out,
       and_18_out, and_19_out, and_20_out, and_21_out, and_22_out, and_23_out, and_24_out, and_25_out,
       and_26_out, and_27_out, and_28_out, and_29_out, and_30_out, and_31_out, and_32_out, and_33_out,
       and_34_out, and_35_out, and_36_out, and_37_out, and_38_out, and_39_out, and_40_out, clock_1_out,
       clock_2_out, not_1_out, not_2_out, or_1_out, or_2_out, or_3_out, or_4_out, or_5_out, or_6_out,
       or_7_out, or_8_out, or_9_out, or_10_out, or_11_out, or_12_out, or_13_out, or_14_out, t_ff_1_q,
       t_ff_1_qn, t_ff_2_qn, t_ff_3_q, t_ff_3_qn, t_ff_4_qn, t_ff_5_q, t_ff_5_qn, t_ff_6_qn, t_ff_7_q,
       t_ff_7_qn, t_ff_8_qn, t_ff_9_q, t_ff_9_qn, t_ff_10_qn;
  wire [4:0] t_ff_2_q;
  wire [19:0] rom_1_data;

  Clock clock_1 (.out(clock_1_out));
  Clock clock_2 (.out(clock_2_out));
  T_Flip_Flop t_ff_1 (.clk(clock_1_out), .T(1'b1), .Q(t_ff_1_q), .Qn(t_ff_1_qn), .reset(or_1_out));  // open: preset, en
  not not_1 (not_1_out, in_1);
  or or_1 (or_1_out, and_20_out, and_17_out);
  T_Flip_Flop t_ff_2 (
    .clk(clock_2_out), .T(1'b1), .Q(t_ff_2_q[0]), .Qn(t_ff_2_qn), .reset(or_2_out));  // open: preset, en
  not not_2 (not_2_out, in_2);
  or or_2 (or_2_out, and_19_out, and_18_out);
  and and_1 (and_1_out, in_1, t_ff_1_q);
  and and_2 (and_2_out, t_ff_1_qn, not_1_out, not_1_out);
  and and_3 (and_3_out, in_2, t_ff_2_q[0]);
  and and_4 (and_4_out, t_ff_2_qn, not_2_out, not_2_out);
  or or_3 (or_3_out, and_1_out, and_2_out);
  or or_4 (or_4_out, and_3_out, and_4_out);
  T_Flip_Flop t_ff_3 (
    .clk(clock_1_out), .T(or_3_out), .Q(t_ff_3_q), .Qn(t_ff_3_qn), .reset(or_5_out));  // open: preset, en
  or or_5 (or_5_out, and_17_out, and_20_out);
  T_Flip_Flop t_ff_4 (
    .clk(clock_2_out), .T(or_4_out), .Q(t_ff_2_q[1]), .Qn(t_ff_4_qn), .reset(or_6_out));  // open: preset, en
  or or_6 (or_6_out, and_18_out, and_19_out);
  and and_5 (and_5_out, and_1_out, t_ff_3_q);
  and and_6 (and_6_out, t_ff_3_qn, and_2_out);
  and and_7 (and_7_out, and_3_out, t_ff_2_q[1]);
  and and_8 (and_8_out, t_ff_4_qn, and_4_out);
  or or_7 (or_7_out, and_5_out, and_6_out);
  or or_8 (or_8_out, and_7_out, and_8_out);
  T_Flip_Flop t_ff_5 (
    .clk(clock_1_out), .T(or_7_out), .Q(t_ff_5_q), .Qn(t_ff_5_qn), .preset(and_20_out), .reset(and_17_out));  // open: en
  T_Flip_Flop t_ff_6 (
    .clk(clock_2_out), .T(or_8_out), .Q(t_ff_2_q[2]), .Qn(t_ff_6_qn), .preset(and_19_out), .reset(and_18_out));  // open: en
  and and_9 (and_9_out, and_5_out, t_ff_5_q);
  and and_10 (and_10_out, t_ff_5_qn, and_6_out);
  and and_11 (and_11_out, and_7_out, t_ff_2_q[2]);
  and and_12 (and_12_out, t_ff_6_qn, and_8_out);
  or or_9 (or_9_out, and_9_out, and_10_out);
  or or_10 (or_10_out, and_11_out, and_12_out);
  T_Flip_Flop t_ff_7 (
    .clk(clock_1_out), .T(or_9_out), .Q(t_ff_7_q), .Qn(t_ff_7_qn), .reset(or_11_out));  // open: preset, en
  or or_11 (or_11_out, and_17_out, and_20_out);
  T_Flip_Flop t_ff_8 (
    .clk(clock_2_out), .T(or_10_out), .Q(t_ff_2_q[3]), .Qn(t_ff_8_qn), .reset(or_12_out));  // open: preset, en
  or or_12 (or_12_out, and_18_out, and_19_out);
  and and_13 (and_13_out, and_9_out, t_ff_7_q);
  and and_14 (and_14_out, t_ff_7_qn, and_10_out);
  and and_15 (and_15_out, and_11_out, t_ff_2_q[3]);
  and and_16 (and_16_out, t_ff_8_qn, and_12_out);
  T_Flip_Flop t_ff_9 (
    .clk(clock_1_out), .T(or_13_out), .Q(t_ff_9_q), .Qn(t_ff_9_qn), .preset(and_20_out), .reset(and_17_out));  // open: en
  or or_13 (or_13_out, and_13_out, and_14_out);
  T_Flip_Flop t_ff_10 (
    .clk(clock_2_out), .T(or_14_out), .Q(t_ff_2_q[4]), .Qn(t_ff_10_qn), .preset(and_19_out),
    .reset(and_18_out));  // open: en
  or or_14 (or_14_out, and_15_out, and_16_out);
  LED _16 (.in(t_ff_9_q));
  LED _8 (.in(t_ff_7_q));
  LED _4 (.in(t_ff_5_q));
  and and_17 (and_17_out, t_ff_9_q, ~t_ff_7_q, t_ff_5_q, ~t_ff_3_q, t_ff_1_q);  // AND_Gate
  LED _16_2 (.in(t_ff_2_q[4]));
  LED _4_2 (.in(t_ff_2_q[2]));
  LED _8_2 (.in(t_ff_2_q[3]));
  and and_18 (and_18_out, t_ff_2_q[4], ~t_ff_2_q[3], t_ff_2_q[2], ~t_ff_2_q[1], t_ff_2_q[0]);  // AND_Gate
  LED _1 (.in(t_ff_1_q));
  LED _2 (.in(t_ff_3_q));
  LED _2_2 (.in(t_ff_2_q[1]));
  LED _1_2 (.in(t_ff_2_q[0]));
  and and_19 (and_19_out, t_ff_2_q[4], t_ff_2_q[3], t_ff_2_q[2], t_ff_2_q[1], t_ff_2_q[0]);
  and and_20 (and_20_out, t_ff_9_q, t_ff_7_q, t_ff_5_q, t_ff_3_q, t_ff_1_q);
  and and_21 (and_21_out, ~t_ff_9_q, ~t_ff_7_q, ~t_ff_5_q, ~t_ff_3_q, t_ff_1_q);  // AND_Gate
  LED led_1 (.in(and_21_out));
  and and_22 (and_22_out, ~t_ff_9_q, ~t_ff_7_q, ~t_ff_5_q, t_ff_3_q, ~t_ff_1_q);  // AND_Gate
  LED led_2 (.in(and_23_out));
  LED led_3 (.in(and_22_out));
  LED led_4 (.in(and_24_out));
  LED led_5 (.in(and_25_out));
  and and_23 (and_23_out, ~t_ff_9_q, ~t_ff_7_q, ~t_ff_5_q, t_ff_3_q, t_ff_1_q);  // AND_Gate
  LED led_6 (.in(and_26_out));
  LED led_7 (.in(and_27_out));
  LED led_8 (.in(and_28_out));
  LED led_9 (.in(and_29_out));
  ROM #(.dataWidth(20)) rom_1 (.addr({3'b000, t_ff_2_q}), .data(rom_1_data));  // open: sel
  and and_24 (and_24_out, ~t_ff_9_q, ~t_ff_7_q, t_ff_5_q, ~t_ff_3_q, t_ff_1_q);  // AND_Gate
  and and_25 (and_25_out, ~t_ff_9_q, ~t_ff_7_q, t_ff_5_q, ~t_ff_3_q, ~t_ff_1_q);  // AND_Gate
  LED led_10 (.in(and_32_out));
  LED led_11 (.in(and_30_out));
  LED led_12 (.in(and_33_out));
  LED led_13 (.in(and_31_out));
  and and_26 (and_26_out, ~t_ff_9_q, ~t_ff_7_q, t_ff_5_q, t_ff_3_q, ~t_ff_1_q);  // AND_Gate
  LED led_14 (.in(and_37_out));
  LED led_15 (.in(and_34_out));
  LED led_16 (.in(and_36_out));
  LED led_17 (.in(and_35_out));
  LED led_18 (.in(rom_1_data[2]));
  LED led_19 (.in(rom_1_data[0]));
  LED led_20 (.in(rom_1_data[1]));
  and and_27 (and_27_out, ~t_ff_9_q, ~t_ff_7_q, t_ff_5_q, t_ff_3_q, t_ff_1_q);  // AND_Gate
  LED led_21 (.in(and_38_out));
  LED led_22 (.in(and_40_out));
  LED led_23 (.in(and_39_out));
  LED led_24 (.in(rom_1_data[6]));
  LED led_25 (.in(rom_1_data[4]));
  LED led_26 (.in(rom_1_data[5]));
  LED led_27 (.in(rom_1_data[3]));
  and and_28 (and_28_out, ~t_ff_9_q, t_ff_7_q, ~t_ff_5_q, ~t_ff_3_q, t_ff_1_q);  // AND_Gate
  and and_29 (and_29_out, ~t_ff_9_q, t_ff_7_q, ~t_ff_5_q, ~t_ff_3_q, ~t_ff_1_q);  // AND_Gate
  LED led_28 (.in(rom_1_data[8]));
  LED led_29 (.in(rom_1_data[7]));
  LED led_30 (.in(rom_1_data[10]));
  LED led_31 (.in(rom_1_data[9]));
  and and_30 (and_30_out, ~t_ff_9_q, t_ff_7_q, ~t_ff_5_q, t_ff_3_q, ~t_ff_1_q);  // AND_Gate
  LED led_32 (.in(rom_1_data[13]));
  LED led_33 (.in(rom_1_data[11]));
  LED led_34 (.in(rom_1_data[12]));
  LED led_35 (.in(rom_1_data[14]));
  and and_31 (and_31_out, ~t_ff_9_q, t_ff_7_q, ~t_ff_5_q, t_ff_3_q, t_ff_1_q);  // AND_Gate
  LED led_36 (.in(rom_1_data[15]));
  LED led_37 (.in(rom_1_data[18]));
  LED led_38 (.in(rom_1_data[17]));
  LED led_39 (.in(rom_1_data[16]));
  and and_32 (and_32_out, ~t_ff_9_q, t_ff_7_q, t_ff_5_q, ~t_ff_3_q, ~t_ff_1_q);  // AND_Gate
  and and_33 (and_33_out, ~t_ff_9_q, t_ff_7_q, t_ff_5_q, ~t_ff_3_q, t_ff_1_q);  // AND_Gate
  LED led_40 (.in(rom_1_data[19]));
  and and_34 (and_34_out, ~t_ff_9_q, t_ff_7_q, t_ff_5_q, t_ff_3_q, ~t_ff_1_q);  // AND_Gate
  and and_35 (and_35_out, ~t_ff_9_q, t_ff_7_q, t_ff_5_q, t_ff_3_q, t_ff_1_q);  // AND_Gate
  and and_36 (and_36_out, t_ff_9_q, ~t_ff_7_q, ~t_ff_5_q, ~t_ff_3_q, t_ff_1_q);  // AND_Gate
  and and_37 (and_37_out, t_ff_9_q, ~t_ff_7_q, ~t_ff_5_q, ~t_ff_3_q, ~t_ff_1_q);  // AND_Gate
  and and_38 (and_38_out, t_ff_9_q, ~t_ff_7_q, ~t_ff_5_q, t_ff_3_q, ~t_ff_1_q);  // AND_Gate
  and and_39 (and_39_out, t_ff_9_q, ~t_ff_7_q, ~t_ff_5_q, t_ff_3_q, t_ff_1_q);  // AND_Gate
  and and_40 (and_40_out, t_ff_9_q, ~t_ff_7_q, t_ff_5_q, ~t_ff_3_q, ~t_ff_1_q);  // AND_Gate

  // Notes on the sheet:
  //   Left Signal - 0
  //   Right Signal - 1
  //   Decoder Method
  //   ROM Method
  //   Data Bus
  //   Data Bus
  //   contents of rom_1 (hex, n*v repeats v):
  //   0 1 2 4 8 10 20 40 80 100 200 400 800 1000 2000 4000 8000 10000 20000 40000 80000
  //   Decoder
endmodule
