// Logisim project problem2.circ as structural Verilog: 2 circuits, main circuit main
module main (
  input  [7:0] From_ADC,
  input  [7:0] Address,
  input  [7:0] Data_In,
  input  [3:0] Control,
  output Actuator_Output,
  output [7:0] Data_Out
);

  wire IO_R_out, IO_W_out, not_1_out, or_1_out, RAM_R_out, RAM_W_out, ROM_R_out, xnor_1_out;

  assign Data_Out = xnor_1_out ? Data_In : 8'bz;  // Controlled_Buffer controlled_buffer_1
  NotExactlyOne xnor_1 (.out(xnor_1_out), .in0(Control[2]), .in1(Control[1]), .in2(Control[0]));
  and ROM_R (ROM_R_out, Control[0], ~Control[1], ~Control[2], ~Control[3]);  // AND_Gate
  ROM rom_1 (.addr(Address), .data(Data_Out), .sel(ROM_R_out));
  and RAM_R (RAM_R_out, ~Control[0], Control[1], ~Control[2], ~Control[3]);  // AND_Gate
  not not_1 (not_1_out, RAM_W_out);
  or or_1 (or_1_out, RAM_R_out, RAM_W_out);
  and RAM_W (RAM_W_out, Control[0], Control[1], ~Control[2], ~Control[3]);  // AND_Gate
  RAM #(.bus("asynch")) ram_1 (.addr(Address), .data(Data_Out), .sel(or_1_out), .ld(not_1_out));  // open: clr
  I_O i_o_1 (
    .Data(Data_Out), .Write(IO_W_out), .Read(IO_R_out), .A(Address), .Actuator_Output(Actuator_Output),
    .Input(From_ADC));
  and IO_R (IO_R_out, ~Control[0], ~Control[1], Control[2], ~Control[3]);  // AND_Gate
  and IO_W (IO_W_out, Control[0], ~Control[1], Control[2], ~Control[3]);  // AND_Gate

  // Notes on the sheet:
  //   contents of rom_1 (hex, n*v repeats v):
  //   12 1 2 3 4 5 6 7 8 9 a b c d e f
endmodule

module I_O (
  input  [7:0] Input,
  input  Write,
  input  Read,
  input  [7:0] A,
  output Actuator_Output,
  output [7:0] Data
);

  wire and_1_out, and_2_out, not_1_out, not_2_out, not_3_out, not_4_out, not_5_out, not_6_out, not_7_out,
       not_8_out, not_9_out, not_10_out;

  not not_1 (not_1_out, Read);
  not not_2 (not_2_out, Write);
  not not_3 (not_3_out, A[0]);
  not not_4 (not_4_out, A[1]);
  not not_5 (not_5_out, A[2]);
  not not_6 (not_6_out, A[3]);
  not not_7 (not_7_out, A[4]);
  not not_8 (not_8_out, A[5]);
  not not_9 (not_9_out, A[6]);
  not not_10 (not_10_out, A[7]);
  assign Actuator_Output = and_1_out ? 1'b1 : 1'bz;  // Controlled_Buffer controlled_buffer_1
  and and_1 (and_1_out, Write, not_1_out, not_3_out, not_4_out, not_5_out, not_6_out, A[4], not_8_out, not_9_out, not_10_out);
  assign Data = and_2_out ? Input : 8'bz;  // Controlled_Buffer controlled_buffer_2
  and and_2 (and_2_out, not_2_out, Read, A[0], A[1], A[2], A[3], A[4], A[5], A[6], A[7]);
endmodule
