// Logisim project problem3.circ as structural Verilog: 8 circuits, main circuit Adder
module Adder (
  input  A,
  input  B,
  input  Cin,
  output Sum,
  output Cout
);

  wire and_1_out, and_2_out, xor_1_out;

  xor xor_1 (xor_1_out, A, B);
  xor xor_2 (Sum, xor_1_out, Cin);
  and and_1 (and_1_out, xor_1_out, Cin);
  and and_2 (and_2_out, A, B);
  or or_1 (Cout, and_1_out, and_2_out);
endmodule

module Subtractor (
  input  A,
  input  B,
  input  Bin,
  output Diff,
  output Bout
);

  wire and_1_out, and_2_out, not_1_out, not_2_out, xor_1_out;

  xor xor_1 (xor_1_out, A, B);
  not not_1 (not_1_out, A);
  not not_2 (not_2_out, xor_1_out);
  xor xor_2 (Diff, xor_1_out, Bin);
  and and_1 (and_1_out, not_2_out, Bin);
  and and_2 (and_2_out, not_1_out, B);
  or or_1 (Bout, and_1_out, and_2_out);
endmodule

module i (
  input  [7:0] in_1,
  input  [7:0] in_2,
  output [7:0] out_3,
  output out_4
);

  wire adder_1_cout, adder_2_cout, adder_3_cout, adder_4_cout, adder_5_cout, adder_6_cout, adder_7_cout;

  Adder adder_1 (.A(in_1[0]), .B(in_2[0]), .Cin(1'b0), .Sum(out_3[0]), .Cout(adder_1_cout));
  Adder adder_2 (.A(in_1[1]), .B(in_2[1]), .Cin(adder_1_cout), .Sum(out_3[1]), .Cout(adder_2_cout));
  Adder adder_3 (.A(in_1[2]), .B(in_2[2]), .Cin(adder_2_cout), .Sum(out_3[2]), .Cout(adder_3_cout));
  Adder adder_4 (.A(in_1[3]), .B(in_2[3]), .Cin(adder_3_cout), .Sum(out_3[3]), .Cout(adder_4_cout));
  Adder adder_5 (.A(in_1[4]), .B(in_2[4]), .Cin(adder_4_cout), .Sum(out_3[4]), .Cout(adder_5_cout));
  Adder adder_6 (.A(in_1[5]), .B(in_2[5]), .Cin(adder_5_cout), .Sum(out_3[5]), .Cout(adder_6_cout));
  Adder adder_7 (.A(in_1[6]), .B(in_2[6]), .Cin(adder_6_cout), .Sum(out_3[6]), .Cout(adder_7_cout));
  Adder adder_8 (.A(in_1[7]), .B(in_2[7]), .Cin(adder_7_cout), .Sum(out_3[7]), .Cout(out_4));

  // Notes on the sheet:
  //   constant
  //   USING ADDER CIRCUIT
  //   does not matter; can throw away 
endmodule

module ii (
  input  [7:0] in_1,
  input  [7:0] in_2,
  output [7:0] out_3,
  output out_4
);

  wire subtractor_1_bout, subtractor_2_bout, subtractor_3_bout, subtractor_4_bout, subtractor_5_bout,
       subtractor_6_bout, subtractor_7_bout;

  Subtractor subtractor_1 (.A(in_1[0]), .B(in_2[0]), .Bin(1'b0), .Diff(out_3[0]), .Bout(subtractor_1_bout));
  Subtractor subtractor_2 (
    .A(in_1[1]), .B(in_2[1]), .Bin(subtractor_1_bout), .Diff(out_3[1]), .Bout(subtractor_2_bout));
  Subtractor subtractor_3 (
    .A(in_1[2]), .B(in_2[2]), .Bin(subtractor_2_bout), .Diff(out_3[2]), .Bout(subtractor_3_bout));
  Subtractor subtractor_4 (
    .A(in_1[3]), .B(in_2[3]), .Bin(subtractor_3_bout), .Diff(out_3[3]), .Bout(subtractor_4_bout));
  Subtractor subtractor_5 (
    .A(in_1[4]), .B(in_2[4]), .Bin(subtractor_4_bout), .Diff(out_3[4]), .Bout(subtractor_5_bout));
  Subtractor subtractor_6 (
    .A(in_1[5]), .B(in_2[5]), .Bin(subtractor_5_bout), .Diff(out_3[5]), .Bout(subtractor_6_bout));
  Subtractor subtractor_7 (
    .A(in_1[6]), .B(in_2[6]), .Bin(subtractor_6_bout), .Diff(out_3[6]), .Bout(subtractor_7_bout));
  Subtractor subtractor_8 (.A(in_1[7]), .B(in_2[7]), .Bin(subtractor_7_bout), .Diff(out_3[7]), .Bout(out_4));

  // Notes on the sheet:
  //   constant
  //   USING SUBTRACTOR CIRCUIT
  //   does not matter; can throw away
endmodule

module iii (
  input  [7:0] A,
  input  [7:0] B,
  output A_B,
  output A_B_2,
  output A_B_3
);

  wire n2_bit_comparator_1_a_b, n2_bit_comparator_1_a_b_3, n2_bit_comparator_2_a_b,
       n2_bit_comparator_2_a_b_3, n2_bit_comparator_3_a_b, n2_bit_comparator_3_a_b_3,
       n2_bit_comparator_4_a_b, n2_bit_comparator_4_a_b_3, n2_bit_comparator_5_a_b,
       n2_bit_comparator_5_a_b_3, n2_bit_comparator_6_a_b, n2_bit_comparator_6_a_b_3;

  _2_bit_Comparator u_2_bit_comparator_1 (
    .A0(A[0]), .A1(A[1]), .B0(B[0]), .B1(B[1]), .A_B(n2_bit_comparator_1_a_b),
    .A_B_3(n2_bit_comparator_1_a_b_3));  // open: A_B_2
  _2_bit_Comparator u_2_bit_comparator_2 (
    .A0(n2_bit_comparator_3_a_b), .A1(A[3]), .B0(n2_bit_comparator_3_a_b_3), .B1(B[3]),
    .A_B(n2_bit_comparator_2_a_b), .A_B_3(n2_bit_comparator_2_a_b_3));  // open: A_B_2
  _2_bit_Comparator u_2_bit_comparator_3 (
    .A0(n2_bit_comparator_1_a_b), .A1(A[2]), .B0(n2_bit_comparator_1_a_b_3), .B1(B[2]),
    .A_B(n2_bit_comparator_3_a_b), .A_B_3(n2_bit_comparator_3_a_b_3));  // open: A_B_2
  _2_bit_Comparator u_2_bit_comparator_4 (
    .A0(n2_bit_comparator_2_a_b), .A1(A[4]), .B0(n2_bit_comparator_2_a_b_3), .B1(B[4]),
    .A_B(n2_bit_comparator_4_a_b), .A_B_3(n2_bit_comparator_4_a_b_3));  // open: A_B_2
  _2_bit_Comparator u_2_bit_comparator_5 (
    .A0(n2_bit_comparator_4_a_b), .A1(A[5]), .B0(n2_bit_comparator_4_a_b_3), .B1(B[5]),
    .A_B(n2_bit_comparator_5_a_b), .A_B_3(n2_bit_comparator_5_a_b_3));  // open: A_B_2
  _2_bit_Comparator u_2_bit_comparator_6 (
    .A0(n2_bit_comparator_5_a_b), .A1(A[6]), .B0(n2_bit_comparator_5_a_b_3), .B1(B[6]),
    .A_B(n2_bit_comparator_6_a_b), .A_B_3(n2_bit_comparator_6_a_b_3));  // open: A_B_2
  _2_bit_Comparator u_2_bit_comparator_7 (
    .A0(n2_bit_comparator_6_a_b), .A1(A[7]), .B0(n2_bit_comparator_6_a_b_3), .B1(B[7]), .A_B(A_B),
    .A_B_2(A_B_2), .A_B_3(A_B_3));

  // Notes on the sheet:
  //   USING 2 BIT COMPARATOR CIRCUIT
endmodule

module _2_bit_Comparator (
  input  A0,
  input  A1,
  input  B0,
  input  B1,
  output A_B,
  output A_B_2,
  output A_B_3
);

  wire and_1_out, and_2_out, and_3_out, and_4_out, and_5_out, and_6_out, and_7_out, and_8_out, and_9_out,
       and_10_out, and_11_out, and_12_out, and_13_out, and_14_out, and_15_out, and_16_out, and_17_out,
       and_18_out, and_19_out, and_20_out, and_21_out, and_22_out, not_1_out, not_2_out, not_3_out,
       not_4_out, not_5_out, not_6_out, not_7_out, not_8_out, not_9_out, not_10_out, not_11_out, not_12_out,
       not_13_out, not_14_out, not_15_out, not_16_out, or_1_out, or_2_out, or_3_out, or_4_out;

  and and_1 (and_1_out, A1, not_1_out);
  not not_1 (not_1_out, B0);
  not not_2 (not_2_out, B1);
  not not_3 (not_3_out, B0);
  not not_4 (not_4_out, A0);
  and and_2 (and_2_out, not_4_out, not_5_out);
  not not_5 (not_5_out, A1);
  not not_6 (not_6_out, B0);
  and and_3 (and_3_out, not_6_out, not_7_out);
  not not_7 (not_7_out, B1);
  not not_8 (not_8_out, A0);
  and and_4 (and_4_out, not_8_out, A1);
  not not_9 (not_9_out, B0);
  and and_5 (and_5_out, not_9_out, B1);
  and and_6 (and_6_out, A0, not_10_out);
  not not_10 (not_10_out, A1);
  and and_7 (and_7_out, B0, not_11_out);
  not not_11 (not_11_out, B1);
  and and_8 (and_8_out, A0, A1);
  and and_9 (and_9_out, B0, B1);
  not not_12 (not_12_out, A0);
  and and_10 (and_10_out, not_12_out, not_13_out);
  not not_13 (not_13_out, A1);
  not not_14 (not_14_out, A0);
  not not_15 (not_15_out, A1);
  and and_11 (and_11_out, and_1_out, not_2_out);
  and and_12 (and_12_out, A0, not_3_out);
  and and_13 (and_13_out, A0, A1);
  not not_16 (not_16_out, B1);
  and and_14 (and_14_out, and_2_out, and_3_out);
  and and_15 (and_15_out, and_4_out, and_5_out);
  and and_16 (and_16_out, and_6_out, and_7_out);
  and and_17 (and_17_out, and_8_out, and_9_out);
  and and_18 (and_18_out, and_10_out, B1);
  and and_19 (and_19_out, not_14_out, B0);
  and and_20 (and_20_out, not_15_out, B0);
  or or_1 (or_1_out, and_11_out, and_12_out);
  and and_21 (and_21_out, and_13_out, not_16_out);
  or or_2 (or_2_out, and_14_out, and_15_out);
  or or_3 (or_3_out, and_16_out, and_17_out);
  or or_4 (or_4_out, and_18_out, and_19_out);
  and and_22 (and_22_out, and_20_out, B1);
  or or_5 (A_B, or_1_out, and_21_out);
  or or_6 (A_B_2, or_2_out, or_3_out);
  or or_7 (A_B_3, or_4_out, and_22_out);
endmodule

module iv__rbs (
  input  [7:0] in_1,
  input  in_2,
  input  in_3,
  input  in_4,
  output [7:0] out_5
);

  wire multiplexer_1_out, multiplexer_2_out, multiplexer_3_out, multiplexer_4_out, multiplexer_5_out,
       multiplexer_6_out, multiplexer_7_out, multiplexer_8_out, multiplexer_9_out, multiplexer_10_out,
       multiplexer_11_out, multiplexer_12_out, multiplexer_13_out, multiplexer_14_out, multiplexer_15_out,
       multiplexer_16_out;

  Multiplexer multiplexer_1 (.in0(in_1[0]), .in1(in_1[1]), .out(multiplexer_1_out), .sel(in_2));  // open: en
  Multiplexer multiplexer_2 (.in0(in_1[1]), .in1(in_1[2]), .out(multiplexer_2_out), .sel(in_2));  // open: en
  Multiplexer multiplexer_3 (.in0(in_1[2]), .in1(in_1[3]), .out(multiplexer_3_out), .sel(in_2));  // open: en
  Multiplexer multiplexer_4 (.in0(in_1[3]), .in1(in_1[4]), .out(multiplexer_4_out), .sel(in_2));  // open: en
  Multiplexer multiplexer_5 (.in0(in_1[4]), .in1(in_1[5]), .out(multiplexer_5_out), .sel(in_2));  // open: en
  Multiplexer multiplexer_6 (.in0(in_1[5]), .in1(in_1[6]), .out(multiplexer_6_out), .sel(in_2));  // open: en
  Multiplexer multiplexer_7 (.in0(in_1[6]), .in1(in_1[7]), .out(multiplexer_7_out), .sel(in_2));  // open: en
  Multiplexer multiplexer_8 (.in0(in_1[7]), .in1(1'b0), .out(multiplexer_8_out), .sel(in_2));  // open: en
  Multiplexer multiplexer_9 (
    .in0(multiplexer_1_out), .in1(multiplexer_3_out), .out(multiplexer_9_out), .sel(in_3));  // open: en
  Multiplexer multiplexer_10 (
    .in0(multiplexer_2_out), .in1(multiplexer_4_out), .out(multiplexer_10_out), .sel(in_3));  // open: en
  Multiplexer multiplexer_11 (
    .in0(multiplexer_3_out), .in1(multiplexer_5_out), .out(multiplexer_11_out), .sel(in_3));  // open: en
  Multiplexer multiplexer_12 (
    .in0(multiplexer_4_out), .in1(multiplexer_6_out), .out(multiplexer_12_out), .sel(in_3));  // open: en
  Multiplexer multiplexer_13 (
    .in0(multiplexer_5_out), .in1(multiplexer_7_out), .out(multiplexer_13_out), .sel(in_3));  // open: en
  Multiplexer multiplexer_14 (
    .in0(multiplexer_6_out), .in1(multiplexer_8_out), .out(multiplexer_14_out), .sel(in_3));  // open: en
  Multiplexer multiplexer_15 (.in0(multiplexer_7_out), .in1(1'b0), .out(multiplexer_15_out), .sel(in_3));  // open: en
  Multiplexer multiplexer_16 (.in0(multiplexer_8_out), .in1(1'b0), .out(multiplexer_16_out), .sel(in_3));  // open: en
  Multiplexer multiplexer_17 (
    .in0(multiplexer_9_out), .in1(multiplexer_13_out), .out(out_5[0]), .sel(in_4));  // open: en
  Multiplexer multiplexer_18 (
    .in0(multiplexer_10_out), .in1(multiplexer_14_out), .out(out_5[1]), .sel(in_4));  // open: en
  Multiplexer multiplexer_19 (
    .in0(multiplexer_11_out), .in1(multiplexer_15_out), .out(out_5[2]), .sel(in_4));  // open: en
  Multiplexer multiplexer_20 (
    .in0(multiplexer_12_out), .in1(multiplexer_16_out), .out(out_5[3]), .sel(in_4));  // open: en
  Multiplexer multiplexer_21 (.in0(multiplexer_13_out), .in1(1'b0), .out(out_5[4]), .sel(in_4));  // open: en
  Multiplexer multiplexer_22 (.in0(multiplexer_14_out), .in1(1'b0), .out(out_5[5]), .sel(in_4));  // open: en
  Multiplexer multiplexer_23 (.in0(multiplexer_15_out), .in1(1'b0), .out(out_5[6]), .sel(in_4));  // open: en
  Multiplexer multiplexer_24 (.in0(multiplexer_16_out), .in1(1'b0), .out(out_5[7]), .sel(in_4));  // open: en

  // Notes on the sheet:
  //   000 keeps it the same while 111 shifts 7 positions to the right
endmodule

module iv__lbs (
  input  in_1,
  input  in_2,
  input  in_3,
  input  [7:0] in_4,
  output [7:0] out_5
);

  wire multiplexer_1_out, multiplexer_2_out, multiplexer_3_out, multiplexer_4_out, multiplexer_5_out,
       multiplexer_6_out, multiplexer_7_out, multiplexer_8_out, multiplexer_9_out, multiplexer_10_out,
       multiplexer_11_out, multiplexer_12_out, multiplexer_13_out, multiplexer_14_out, multiplexer_15_out,
       multiplexer_16_out;

  Multiplexer multiplexer_1 (.in0(in_4[0]), .in1(1'b0), .out(multiplexer_1_out), .sel(in_1));  // open: en
  Multiplexer multiplexer_2 (.in0(in_4[1]), .in1(in_4[0]), .out(multiplexer_2_out), .sel(in_1));  // open: en
  Multiplexer multiplexer_3 (.in0(in_4[2]), .in1(in_4[1]), .out(multiplexer_3_out), .sel(in_1));  // open: en
  Multiplexer multiplexer_4 (.in0(in_4[3]), .in1(in_4[2]), .out(multiplexer_4_out), .sel(in_1));  // open: en
  Multiplexer multiplexer_5 (.in0(in_4[4]), .in1(in_4[3]), .out(multiplexer_5_out), .sel(in_1));  // open: en
  Multiplexer multiplexer_6 (.in0(in_4[5]), .in1(in_4[4]), .out(multiplexer_6_out), .sel(in_1));  // open: en
  Multiplexer multiplexer_7 (.in0(in_4[6]), .in1(in_4[5]), .out(multiplexer_7_out), .sel(in_1));  // open: en
  Multiplexer multiplexer_8 (.in0(in_4[7]), .in1(in_4[6]), .out(multiplexer_8_out), .sel(in_1));  // open: en
  Multiplexer multiplexer_9 (.in0(multiplexer_1_out), .in1(1'b0), .out(multiplexer_9_out), .sel(in_2));  // open: en
  Multiplexer multiplexer_10 (.in0(multiplexer_2_out), .in1(1'b0), .out(multiplexer_10_out), .sel(in_2));  // open: en
  Multiplexer multiplexer_11 (
    .in0(multiplexer_3_out), .in1(multiplexer_1_out), .out(multiplexer_11_out), .sel(in_2));  // open: en
  Multiplexer multiplexer_12 (
    .in0(multiplexer_4_out), .in1(multiplexer_2_out), .out(multiplexer_12_out), .sel(in_2));  // open: en
  Multiplexer multiplexer_13 (
    .in0(multiplexer_5_out), .in1(multiplexer_3_out), .out(multiplexer_13_out), .sel(in_2));  // open: en
  Multiplexer multiplexer_14 (
    .in0(multiplexer_6_out), .in1(multiplexer_4_out), .out(multiplexer_14_out), .sel(in_2));  // open: en
  Multiplexer multiplexer_15 (
    .in0(multiplexer_7_out), .in1(multiplexer_5_out), .out(multiplexer_15_out), .sel(in_2));  // open: en
  Multiplexer multiplexer_16 (
    .in0(multiplexer_8_out), .in1(multiplexer_6_out), .out(multiplexer_16_out), .sel(in_2));  // open: en
  Multiplexer multiplexer_17 (.in0(multiplexer_9_out), .in1(1'b0), .out(out_5[0]), .sel(in_3));  // open: en
  Multiplexer multiplexer_18 (.in0(multiplexer_10_out), .in1(1'b0), .out(out_5[1]), .sel(in_3));  // open: en
  Multiplexer multiplexer_19 (.in0(multiplexer_11_out), .in1(1'b0), .out(out_5[2]), .sel(in_3));  // open: en
  Multiplexer multiplexer_20 (.in0(multiplexer_12_out), .in1(1'b0), .out(out_5[3]), .sel(in_3));  // open: en
  Multiplexer multiplexer_21 (
    .in0(multiplexer_13_out), .in1(multiplexer_9_out), .out(out_5[4]), .sel(in_3));  // open: en
  Multiplexer multiplexer_22 (
    .in0(multiplexer_14_out), .in1(multiplexer_10_out), .out(out_5[5]), .sel(in_3));  // open: en
  Multiplexer multiplexer_23 (
    .in0(multiplexer_15_out), .in1(multiplexer_11_out), .out(out_5[6]), .sel(in_3));  // open: en
  Multiplexer multiplexer_24 (
    .in0(multiplexer_16_out), .in1(multiplexer_12_out), .out(out_5[7]), .sel(in_3));  // open: en

  // Notes on the sheet:
  //   000 keeps it the same while 111 shifts 7 positions to the left
endmodule
