// Logisim project cpu.circ as structural Verilog: 5 circuits, main circuit CPU
// Mem
module Memory (
  input  [7:0] Address,
  input  [7:0] Data_In,
  input  [1:0] Operation,
  output [7:0] Data_Out
);

  wire not_1_out, or_1_out, RAM_R_out, RAM_W_out, ROM_R_out;

  assign Data_Out = RAM_W_out ? Data_In : 8'bz;  // Controlled_Buffer controlled_buffer_1
  and ROM_R (ROM_R_out, Operation[0], ~Operation[1]);  // AND_Gate
  ROM rom_1 (.addr(Address), .data(Data_Out), .sel(ROM_R_out));
  and RAM_R (RAM_R_out, ~Operation[0], Operation[1]);  // AND_Gate
  not not_1 (not_1_out, RAM_W_out);
  or or_1 (or_1_out, RAM_R_out, RAM_W_out);
  and RAM_W (RAM_W_out, Operation[0], Operation[1]);
  RAM #(.bus("asynch")) ram_1 (.addr(Address), .data(Data_Out), .sel(or_1_out), .ld(not_1_out));  // open: clr

  // Notes on the sheet:
  //   contents of rom_1 (hex, n*v repeats v):
  //   4 0 1 4 4 2 4 8 5 4 1 3 2 31 0 4 2 3 2 31 1 4 3 3 2 31 2 4 4 3 2 31 3 4 4 3 2 32 0 4 3 3 2 32 1 4 2
  //   3 2 32 2 4 1 3 2 32 3 3 31 0 3 42 0 5 34 2 45 0 3 31 1 3 42 1 5 34 2 45 1 3 31 2 3 42 2 5 34 2 45 2
  //   3 31 3 3 42 3 5 34 2 45 3 1
endmodule

module CPU (
);

  wire A_Overflow, ADD, and_1_out, and_2_out, and_3_out, and_4_out, and_5_out, and_6_out, and_7_out,
       and_8_out, and_9_out, and_10_out, and_11_out, and_12_out, and_13_out, Clear, clock_1_byte1,
       clock_1_byte2, clock_1_fetch_reg_1, clock_1_fetch_reg_2, clock_1_instruction, Decode, Execute,
       HALT_out, MEMLD, MEMSET, NOP, PC_Update, R_dR, R_dW, REGSET, Write;
  wire [1:0] A_Mode, M_Select;
  wire [3:0] R_Addr, rA_R, rA_W, rB_R, rB_W;
  wire [7:0] A_In1, A_In2, A_Out, adder_1_out, adder_2_out, DataByte1, DataByte2, ExecResult_R, ExecResult_W,
       M_Addr, M_In, M_Out, nPC_In, nPC_Out, PC_Out, pci_R, pci_W, pci_W_t, R_In, R_Out, rA_val, rB_val,
       register_8_q, val_R, val_W;
  wire [7:4] controlled_buffer_17_out;

  Register #(.trigger("high")) register_1 (.D(nPC_In), .Q(nPC_Out), .clk(Write), .clr(Clear));  // open: en
  Register #(.trigger("high")) register_2 (.D(ExecResult_W), .Q(ExecResult_R), .clk(Execute), .clr(Clear));  // open: en
  Register #(.width(4), .trigger("high")) register_3 (.D(rA_W), .Q(rA_R), .clk(Decode), .clr(Clear));  // open: en
  Register #(.width(4), .trigger("high")) register_4 (.D(rB_W), .Q(rB_R), .clk(Decode), .clr(Clear));  // open: en
  Register #(.trigger("high")) register_5 (.D(val_W), .Q(val_R), .clk(Decode), .clr(Clear));  // open: en
  Register #(.trigger("high")) register_6 (.D(pci_W_t), .Q(pci_R), .clk(Decode), .clr(Clear));  // open: en
  Clock clock_1 (
    .Clear(Clear), .Instruction(clock_1_instruction), .Byte1(clock_1_byte1), .Byte2(clock_1_byte2),
    .Decode(Decode), .Fetch_Reg_1(clock_1_fetch_reg_1), .Fetch_Reg_2(clock_1_fetch_reg_2), .Execute(Execute),
    .Write(Write), .Update_PC(PC_Update), .Halt(HALT_out));
  Memory memory_1 (.Address(M_Addr), .Data_Out(M_Out), .Data_In(M_In), .Operation(M_Select));
  Register_File register_file_1 (.Write_Data(R_In), .Addr(R_Addr), .Read_Data(R_Out), .Read(R_dR), .Write(R_dW));
  ALU alu_1 (.Input1(A_In1), .Input2(A_In2), .Mode(A_Mode), .Output(A_Out), .Overflow(A_Overflow));
  assign M_Select = clock_1_instruction ? 2'b01 : 2'bz;  // Controlled_Buffer controlled_buffer_1
  assign M_Select = clock_1_byte1 ? 2'b01 : 2'bz;  // Controlled_Buffer controlled_buffer_2
  assign M_Select = clock_1_byte2 ? 2'b01 : 2'bz;  // Controlled_Buffer controlled_buffer_3
  Register #(.trigger("high")) register_7 (.D(nPC_Out), .Q(PC_Out), .clk(PC_Update));  // open: en, clr
  assign M_Addr = clock_1_instruction ? PC_Out : 8'bz;  // Controlled_Buffer controlled_buffer_4
  Adder adder_1 (.a(PC_Out), .b(8'h1), .out(adder_1_out));  // open: cin, cout
  assign M_Addr = clock_1_byte1 ? adder_1_out : 8'bz;  // Controlled_Buffer controlled_buffer_5
  assign M_Addr = clock_1_byte2 ? adder_2_out : 8'bz;  // Controlled_Buffer controlled_buffer_6
  Adder adder_2 (.a(PC_Out), .b(8'h2), .out(adder_2_out));  // open: cin, cout
  or or_1 (R_dR, clock_1_fetch_reg_1, clock_1_fetch_reg_2);
  assign R_Addr = clock_1_fetch_reg_1 ? rA_R : 4'bz;  // Controlled_Buffer controlled_buffer_7
  assign R_Addr = clock_1_fetch_reg_2 ? rB_R : 4'bz;  // Controlled_Buffer controlled_buffer_8
  and HALT (HALT_out, register_8_q[0], ~register_8_q[1], ~register_8_q[2], ~register_8_q[3], ~register_8_q[4], ~register_8_q[5], ~register_8_q[6], ~register_8_q[7]);  // AND_Gate
  Register #(.trigger("high")) register_8 (
    .D(M_Out), .Q(register_8_q), .clk(clock_1_instruction), .clr(Clear));  // open: en
  Register #(.trigger("high")) register_9 (.D(M_Out), .Q(DataByte1), .clk(clock_1_byte1), .clr(Clear));  // open: en
  Register #(.trigger("high")) register_10 (.D(M_Out), .Q(DataByte2), .clk(clock_1_byte2), .clr(Clear));  // open: en
  and u_MEMSET (MEMSET, ~register_8_q[0], register_8_q[1], ~register_8_q[2], ~register_8_q[3], ~register_8_q[4], ~register_8_q[5], ~register_8_q[6], ~register_8_q[7]);  // AND_Gate
  and u_MEMLD (MEMLD, register_8_q[0], register_8_q[1], ~register_8_q[2], ~register_8_q[3], ~register_8_q[4], ~register_8_q[5], ~register_8_q[6], ~register_8_q[7]);  // AND_Gate
  Register #(.trigger("high")) register_11 (.D(R_Out), .Q(rA_val), .clk(clock_1_fetch_reg_1), .clr(Clear));  // open: en
  and u_REGSET (REGSET, ~register_8_q[0], ~register_8_q[1], register_8_q[2], ~register_8_q[3], ~register_8_q[4], ~register_8_q[5], ~register_8_q[6], ~register_8_q[7]);  // AND_Gate
  Register #(.trigger("high")) register_12 (.D(R_Out), .Q(rB_val), .clk(clock_1_fetch_reg_2), .clr(Clear));  // open: en
  and u_ADD (ADD, register_8_q[0], ~register_8_q[1], register_8_q[2], ~register_8_q[3], ~register_8_q[4], ~register_8_q[5], ~register_8_q[6], ~register_8_q[7]);  // AND_Gate
  nor nor_1 (NOP, HALT_out, MEMSET, MEMLD, REGSET, ADD);
  and and_1 (and_1_out, NOP, Decode);
  assign pci_W = and_1_out ? 8'h1 : 8'bz;  // Controlled_Buffer controlled_buffer_9
  and and_2 (and_2_out, MEMSET, Decode);
  assign {rB_W, rA_W} = and_2_out ? DataByte1 : 8'bz;  // Controlled_Buffer controlled_buffer_10
  assign val_W = and_2_out ? DataByte2 : 8'bz;  // Controlled_Buffer controlled_buffer_11
  assign pci_W = and_2_out ? 8'h3 : 8'bz;  // Controlled_Buffer controlled_buffer_12
  and and_3 (and_3_out, MEMLD, Decode);
  assign {rB_W, rA_W} = and_3_out ? DataByte1 : 8'bz;  // Controlled_Buffer controlled_buffer_13
  assign val_W = and_3_out ? DataByte2 : 8'bz;  // Controlled_Buffer controlled_buffer_14
  assign pci_W = and_3_out ? 8'h3 : 8'bz;  // Controlled_Buffer controlled_buffer_15
  and and_4 (and_4_out, REGSET, Decode);
  assign val_W = and_4_out ? DataByte1 : 8'bz;  // Controlled_Buffer controlled_buffer_16
  assign {controlled_buffer_17_out, rA_W} = and_4_out ? DataByte2 : 8'bz;  // Controlled_Buffer controlled_buffer_17
  assign pci_W = and_4_out ? 8'h3 : 8'bz;  // Controlled_Buffer controlled_buffer_18
  and and_5 (and_5_out, ADD, Decode);
  assign {rB_W, rA_W} = and_5_out ? DataByte1 : 8'bz;  // Controlled_Buffer controlled_buffer_19
  assign pci_W = and_5_out ? 8'h2 : 8'bz;  // Controlled_Buffer controlled_buffer_20
  and and_6 (and_6_out, MEMSET, Execute);
  assign A_In1 = and_6_out ? rA_val : 8'bz;  // Controlled_Buffer controlled_buffer_21
  assign A_In2 = and_6_out ? val_R : 8'bz;  // Controlled_Buffer controlled_buffer_22
  assign A_Mode = and_6_out ? 2'b01 : 2'bz;  // Controlled_Buffer controlled_buffer_23
  assign ExecResult_W = and_6_out ? A_Out : 8'bz;  // Controlled_Buffer controlled_buffer_24
  and and_7 (and_7_out, MEMLD, Execute);
  assign A_In1 = and_7_out ? rA_val : 8'bz;  // Controlled_Buffer controlled_buffer_25
  assign A_In2 = and_7_out ? val_R : 8'bz;  // Controlled_Buffer controlled_buffer_26
  assign A_Mode = and_7_out ? 2'b01 : 2'bz;  // Controlled_Buffer controlled_buffer_27
  assign M_Addr = and_7_out ? A_Out : 8'bz;  // Controlled_Buffer controlled_buffer_28
  assign ExecResult_W = and_7_out ? M_Out : 8'bz;  // Controlled_Buffer controlled_buffer_29
  assign M_Select = and_7_out ? 2'b10 : 2'bz;  // Controlled_Buffer controlled_buffer_30
  and and_8 (and_8_out, REGSET, Execute);
  assign ExecResult_W = and_8_out ? val_R : 8'bz;  // Controlled_Buffer controlled_buffer_31
  and and_9 (and_9_out, ADD, Execute);
  assign A_In1 = and_9_out ? rA_val : 8'bz;  // Controlled_Buffer controlled_buffer_32
  assign A_In2 = and_9_out ? rB_val : 8'bz;  // Controlled_Buffer controlled_buffer_33
  assign A_Mode = and_9_out ? 2'b01 : 2'bz;  // Controlled_Buffer controlled_buffer_34
  assign ExecResult_W = and_9_out ? A_Out : 8'bz;  // Controlled_Buffer controlled_buffer_35
  and and_10 (and_10_out, MEMSET, Write);
  and and_11 (and_11_out, MEMLD, Write);
  and and_12 (and_12_out, REGSET, Write);
  and and_13 (and_13_out, ADD, Write);
  assign A_In1 = Write ? pci_R : 8'bz;  // Controlled_Buffer controlled_buffer_36
  assign A_In2 = Write ? PC_Out : 8'bz;  // Controlled_Buffer controlled_buffer_37
  assign A_Mode = Write ? 2'b01 : 2'bz;  // Controlled_Buffer controlled_buffer_38
  assign nPC_In = Write ? A_Out : 8'bz;  // Controlled_Buffer controlled_buffer_39
  assign M_Addr = and_10_out ? ExecResult_R : 8'bz;  // Controlled_Buffer controlled_buffer_40
  assign M_In = and_10_out ? rB_val : 8'bz;  // Controlled_Buffer controlled_buffer_41
  assign M_Select = and_10_out ? 2'b11 : 2'bz;  // Controlled_Buffer controlled_buffer_42
  assign R_In = and_11_out ? ExecResult_R : 8'bz;  // Controlled_Buffer controlled_buffer_43
  assign R_Addr = and_11_out ? rB_R : 4'bz;  // Controlled_Buffer controlled_buffer_44
  assign R_In = and_12_out ? ExecResult_R : 8'bz;  // Controlled_Buffer controlled_buffer_45
  assign R_Addr = and_12_out ? rA_R : 4'bz;  // Controlled_Buffer controlled_buffer_46
  assign R_In = and_13_out ? ExecResult_R : 8'bz;  // Controlled_Buffer controlled_buffer_47
  assign R_Addr = and_13_out ? rA_R : 4'bz;  // Controlled_Buffer controlled_buffer_48
  ExactlyOne xor_1 (.out(R_dW), .in0(and_11_out), .in1(and_12_out), .in2(and_13_out));
endmodule

// Reg
module Register_File (
  input  [7:0] Write_Data,
  input  Write,
  input  Read,
  input  [3:0] Addr,
  output [7:0] Read_Data
);

  wire and_1_out, and_2_out, and_3_out, and_4_out, and_5_out, controlled_buffer_2_out,
       controlled_buffer_3_out, controlled_buffer_5_out, controlled_buffer_6_out, controlled_buffer_7_out,
       controlled_buffer_8_out, controlled_buffer_10_out, controlled_buffer_12_out, controlled_buffer_13_out,
       controlled_buffer_15_out;
  wire [7:0] register_1_q, register_2_q, register_3_q, register_4_q, register_5_q;

  Register #(.trigger("high")) register_1 (
    .D(Write_Data), .Q(register_1_q), .clk(controlled_buffer_2_out));  // open: en, clr
  assign Read_Data = controlled_buffer_3_out ? register_1_q : 8'bz;  // Controlled_Buffer controlled_buffer_1
  assign controlled_buffer_2_out = Write ? and_1_out : 1'bz;  // Controlled_Buffer controlled_buffer_2
  assign controlled_buffer_3_out = Read ? and_1_out : 1'bz;  // Controlled_Buffer controlled_buffer_3
  and and_1 (and_1_out, Addr[0], ~Addr[1], ~Addr[2], ~Addr[3]);  // AND_Gate
  assign Read_Data = controlled_buffer_6_out ? register_2_q : 8'bz;  // Controlled_Buffer controlled_buffer_4
  Register #(.trigger("high")) register_2 (
    .D(Write_Data), .Q(register_2_q), .clk(controlled_buffer_5_out));  // open: en, clr
  assign controlled_buffer_5_out = Write ? and_2_out : 1'bz;  // Controlled_Buffer controlled_buffer_5
  assign controlled_buffer_6_out = Read ? and_2_out : 1'bz;  // Controlled_Buffer controlled_buffer_6
  and and_2 (and_2_out, ~Addr[0], Addr[1], ~Addr[2], ~Addr[3]);  // AND_Gate
  Register #(.trigger("high")) register_3 (
    .D(Write_Data), .Q(register_3_q), .clk(controlled_buffer_7_out));  // open: en, clr
  assign controlled_buffer_7_out = Write ? and_3_out : 1'bz;  // Controlled_Buffer controlled_buffer_7
  assign controlled_buffer_8_out = Read ? and_3_out : 1'bz;  // Controlled_Buffer controlled_buffer_8
  and and_3 (and_3_out, Addr[0], Addr[1], ~Addr[2], ~Addr[3]);  // AND_Gate
  assign Read_Data = controlled_buffer_8_out ? register_3_q : 8'bz;  // Controlled_Buffer controlled_buffer_9
  Register #(.trigger("high")) register_4 (
    .D(Write_Data), .Q(register_4_q), .clk(controlled_buffer_10_out));  // open: en, clr
  assign controlled_buffer_10_out = Write ? and_4_out : 1'bz;  // Controlled_Buffer controlled_buffer_10
  and and_4 (and_4_out, ~Addr[0], ~Addr[1], Addr[2], ~Addr[3]);  // AND_Gate
  assign Read_Data = controlled_buffer_13_out ? register_4_q : 8'bz;  // Controlled_Buffer controlled_buffer_11
  assign controlled_buffer_12_out = Write ? and_5_out : 1'bz;  // Controlled_Buffer controlled_buffer_12
  assign controlled_buffer_13_out = Read ? and_4_out : 1'bz;  // Controlled_Buffer controlled_buffer_13
  and and_5 (and_5_out, Addr[0], ~Addr[1], Addr[2], ~Addr[3]);  // AND_Gate
  Register #(.trigger("high")) register_5 (
    .D(Write_Data), .Q(register_5_q), .clk(controlled_buffer_12_out));  // open: en, clr
  assign Read_Data = controlled_buffer_15_out ? register_5_q : 8'bz;  // Controlled_Buffer controlled_buffer_14
  assign controlled_buffer_15_out = Read ? and_5_out : 1'bz;  // Controlled_Buffer controlled_buffer_15

  // Notes on the sheet:
  //   R1
  //   R2
  //   R3
  //   R4
  //   R5
endmodule

module Clock (
  input  Halt,
  output Clear,
  output Instruction,
  output Byte1,
  output Byte2,
  output Decode,
  output Fetch_Reg_1,
  output Fetch_Reg_2,
  output Execute,
  output Write,
  output Update_PC
);

  wire and_1_out, clock_1_out, not_1_out;
  wire [3:0] adder_1_out, controlled_buffer_1_out, register_1_q;

  Clock_part clock_1 (.out(clock_1_out));
  Register #(.width(4)) register_1 (.D(controlled_buffer_1_out), .Q(register_1_q), .clk(and_1_out));  // open: en, clr
  and and_1 (and_1_out, clock_1_out, ~Halt);  // AND_Gate
  Adder #(.width(4)) adder_1 (.a(register_1_q), .b(4'b0001), .out(adder_1_out));  // open: cin, cout
  assign controlled_buffer_1_out = not_1_out ? adder_1_out : 4'bz;  // Controlled_Buffer controlled_buffer_1
  not not_1 (not_1_out, Update_PC);
  assign controlled_buffer_1_out = Update_PC ? 4'b0000 : 4'bz;  // Controlled_Buffer controlled_buffer_2
  Decoder #(.select(4)) decoder_1 (
    .out0(Clear), .out1(Instruction), .out2(Byte1), .out3(Byte2), .out4(Decode), .out5(Fetch_Reg_1),
    .out6(Fetch_Reg_2), .out7(Execute), .out8(Write), .out9(Update_PC), .sel(register_1_q));  // open: out10, out11, out12, out13, out14, out15, en
endmodule

module ALU (
  input  [7:0] Input1,
  input  [7:0] Input2,
  input  [1:0] Mode,
  output [7:0] Output,
  output Overflow
);

  wire adder_1_cout, decoder_1_out0, decoder_1_out1, decoder_1_out2, subtractor_1_bout;
  wire [7:0] adder_1_out, subtractor_1_out;

  assign Output = decoder_1_out0 ? {8{1'b0}} : 8'bz;  // Controlled_Buffer controlled_buffer_1
  assign Overflow = decoder_1_out0 ? 1'b0 : 1'bz;  // Controlled_Buffer controlled_buffer_2
  Adder adder_1 (.a(Input1), .b(Input2), .out(adder_1_out), .cout(adder_1_cout));  // open: cin
  assign Output = decoder_1_out1 ? adder_1_out : 8'bz;  // Controlled_Buffer controlled_buffer_3
  assign Overflow = decoder_1_out1 ? adder_1_cout : 1'bz;  // Controlled_Buffer controlled_buffer_4
  Decoder #(.select(2)) decoder_1 (
    .out0(decoder_1_out0), .out1(decoder_1_out1), .out2(decoder_1_out2), .sel(Mode));  // open: out3, en
  Subtractor subtractor_1 (.a(Input1), .b(Input2), .out(subtractor_1_out), .bout(subtractor_1_bout));  // open: bin
  assign Overflow = decoder_1_out2 ? subtractor_1_bout : 1'bz;  // Controlled_Buffer controlled_buffer_5
  assign Output = decoder_1_out2 ? subtractor_1_out : 8'bz;  // Controlled_Buffer controlled_buffer_6
endmodule
